// Digital circuit lab01.dig as structural Verilog
module lab01 (
  input  clk
);

  wire u_gen_tick_tick;

  gen_tick #(.applicationType("IVERILOG"), .CodeFile("/workspaces/Lab01-ClocksAndTestBenches/gen_tick.v")) u_gen_tick (
    .src_clk(clk), .enable(1'b1), .tick(u_gen_tick_tick));
  LED led_1 (.in(u_gen_tick_tick));

  // Notes on the sheet:
  //   clk: Hz: 5000
endmodule
